// Logisim project Multiplexores.circ as structural Verilog: 5 circuits, main circuit main
module main (
  input  in_1,
  input  in_2,
  input  in_3,
  input  in_4,
  input  in_5,
  input  in_6,
  input  in_7,
  input  in_8,
  input  in_9,
  output out_10,
  output out_11,
  output out_12
);

  Multiplexor multiplexor_1 (.A(in_1), .B(in_2), .C(in_3), .D(in_4), .i1(in_5), .i0(in_6), .Q(out_10));
  // FullAdder fulladder_1: pin names not known; wires that end beside it: in_7, in_8, in_9, out_11, out_12
endmodule

module Multiplexor (
  input  A,
  input  B,
  input  C,
  input  D,
  input  i1,
  input  i0,
  output Q
);

  wire nand_1_out, nand_2_out, nand_3_out, nand_4_out, nand_5_out, nand_6_out;

  nand nand_1 (nand_1_out, i1, i1);
  nand nand_2 (nand_2_out, i0, i0);
  nand nand_3 (nand_3_out, A, nand_1_out, nand_2_out);
  nand nand_4 (nand_4_out, B, nand_1_out, i0);
  nand nand_5 (nand_5_out, C, nand_2_out, i1);
  nand nand_6 (nand_6_out, D, i1, i0);
  nand nand_7 (Q, nand_3_out, nand_4_out, nand_5_out, nand_6_out);

  // Notes on the sheet:
  //   i11
  //   A1
  //   B1
  //   i01
  //   C1
  //   D1
  //   Q2
  //   Q3
  //   Q4
  //   Q5
  //   Q0
  //   Q1
endmodule

module HalfAdder (
  input  A,
  input  B,
  output Q,
  output Cout
);

  Multiplexor multiplexor_1 (.A(1'b0), .B(1'b1), .C(1'b1), .D(1'b0), .i1(A), .i0(B), .Q(Q));
  Multiplexor multiplexor_2 (.A(1'b0), .B(1'b0), .C(1'b0), .D(1'b1), .i1(A), .i0(B), .Q(Cout));
endmodule

module FullAdder (
  input  C,
  input  A,
  input  B,
  output sum,
  output carry
);

  wire not_1_out;

  not not_1 (not_1_out, C);
  Multiplexor multiplexor_1 (.A(C), .B(not_1_out), .C(not_1_out), .D(C), .i1(A), .i0(B), .Q(sum));
  Multiplexor multiplexor_2 (.A(1'b0), .B(C), .C(C), .D(1'b1), .i1(A), .i0(B), .Q(carry));
endmodule

module Multiplier (
  input  A3,
  input  A2,
  input  A1,
  input  A0,
  input  B3,
  input  B2,
  input  B1,
  input  B0,
  output Z7,
  output Z6,
  output Z5,
  output Z4,
  output Z3,
  output Z2,
  output Z1,
  output Z0
);

  wire multiplexer_8_out, multiplexer_12_out, multiplexer_14_out, multiplexer_16_out, multiplexer_18_out,
       multiplexer_20_out, multiplexer_22_out, multiplexer_24_out, multiplexer_26_out, not_1_out, not_2_out,
       not_3_out, not_4_out, not_5_out, not_6_out, not_7_out, not_8_out, not_9_out;
  wire [1:0] and_1_out, and_2_out, and_4_out, and_5_out, and_6_out, and_9_out, multiplexer_17_out,
       nand_1_out, nand_2_out, nand_4_out, nand_5_out;
  wire [1:1] multiplexer_4_out, nand_3_out;

  Multiplexer #(.select(2), .enable("false")) multiplexer_1 (
    .in0(1'b0), .in1(1'b1), .in2(1'b1), .in3(1'b0), .out(Z7), .sel({multiplexer_4_out[1], 1'b1}));
  Multiplexer #(.select(2), .enable("false")) multiplexer_2 (
    .in0(1'b0), .in1(1'b0), .in2(1'b0), .in3(1'b1), .sel({multiplexer_4_out[1], 1'b1}));  // open: out
  Multiplexer #(.select(2), .enable("false")) multiplexer_3 (
    .in0(multiplexer_8_out), .in1(not_1_out), .in2(not_1_out), .in3(multiplexer_8_out), .out(Z6),
    .sel(and_1_out));
  Multiplexer #(.select(2), .enable("false")) multiplexer_4 (
    .in0(1'b0), .in1(multiplexer_8_out), .in2(multiplexer_8_out), .in3(1'b1), .out(multiplexer_4_out[1]),
    .sel(and_1_out));
  Multiplexer #(.select(2), .enable("false")) multiplexer_5 (
    .in0(multiplexer_12_out), .in1(not_2_out), .in2(not_2_out), .in3(multiplexer_12_out),
    .out(nand_2_out[1]), .sel(nand_1_out));
  Multiplexer #(.select(2), .enable("false")) multiplexer_6 (
    .in0(1'b0), .in1(multiplexer_12_out), .in2(multiplexer_12_out), .in3(1'b1), .out(and_1_out[1]),
    .sel(nand_1_out));
  and and_1 (and_1_out[0], A3, B3);
  not not_1 (not_1_out, multiplexer_8_out);
  Multiplexer #(.select(2), .enable("false")) multiplexer_7 (
    .in0(multiplexer_14_out), .in1(not_3_out), .in2(not_3_out), .in3(multiplexer_14_out), .out(Z5),
    .sel(nand_2_out));
  Multiplexer #(.select(2), .enable("false")) multiplexer_8 (
    .in0(1'b0), .in1(multiplexer_14_out), .in2(multiplexer_14_out), .in3(1'b1), .out(multiplexer_8_out),
    .sel(nand_2_out));
  nand nand_1 (nand_1_out[0], A3, B2);
  not not_2 (not_2_out, multiplexer_12_out);
  nand nand_2 (nand_2_out[0], A2, B3);
  not not_3 (not_3_out, multiplexer_14_out);
  not not_4 (not_4_out, multiplexer_16_out);
  Multiplexer #(.select(2), .enable("false")) multiplexer_9 (
    .in0(multiplexer_16_out), .in1(not_4_out), .in2(not_4_out), .in3(multiplexer_16_out), .out(and_2_out[1]),
    .sel({nand_3_out[1], 1'b1}));
  Multiplexer #(.select(2), .enable("false")) multiplexer_10 (
    .in0(1'b0), .in1(multiplexer_16_out), .in2(multiplexer_16_out), .in3(1'b1), .out(nand_1_out[1]),
    .sel({nand_3_out[1], 1'b1}));
  not not_5 (not_5_out, multiplexer_18_out);
  Multiplexer #(.select(2), .enable("false")) multiplexer_11 (
    .in0(multiplexer_18_out), .in1(not_5_out), .in2(not_5_out), .in3(multiplexer_18_out),
    .out(nand_4_out[1]), .sel(and_2_out));
  Multiplexer #(.select(2), .enable("false")) multiplexer_12 (
    .in0(1'b0), .in1(multiplexer_18_out), .in2(multiplexer_18_out), .in3(1'b1), .out(multiplexer_12_out),
    .sel(and_2_out));
  not not_6 (not_6_out, multiplexer_20_out);
  Multiplexer #(.select(2), .enable("false")) multiplexer_13 (
    .in0(multiplexer_20_out), .in1(not_6_out), .in2(not_6_out), .in3(multiplexer_20_out), .out(Z4),
    .sel(nand_4_out));
  Multiplexer #(.select(2), .enable("false")) multiplexer_14 (
    .in0(1'b0), .in1(multiplexer_20_out), .in2(multiplexer_20_out), .in3(1'b1), .out(multiplexer_14_out),
    .sel(nand_4_out));
  nand nand_3 (nand_3_out[1], A3, B1);
  Multiplexer #(.select(2), .enable("false")) multiplexer_15 (
    .in0(multiplexer_22_out), .in1(not_7_out), .in2(not_7_out), .in3(multiplexer_22_out), .out(and_4_out[1]),
    .sel(nand_5_out));
  Multiplexer #(.select(2), .enable("false")) multiplexer_16 (
    .in0(1'b0), .in1(multiplexer_22_out), .in2(multiplexer_22_out), .in3(1'b1), .out(multiplexer_16_out),
    .sel(nand_5_out));
  and and_2 (and_2_out[0], A2, B2);
  Multiplexer #(.select(2), .enable("false")) multiplexer_17 (
    .in0(multiplexer_24_out), .in1(not_8_out), .in2(not_8_out), .in3(multiplexer_24_out),
    .out(multiplexer_17_out[0]), .sel(and_4_out));
  Multiplexer #(.select(2), .enable("false")) multiplexer_18 (
    .in0(1'b0), .in1(multiplexer_24_out), .in2(multiplexer_24_out), .in3(1'b1), .out(multiplexer_18_out),
    .sel(and_4_out));
  nand nand_4 (nand_4_out[0], A1, B3);
  Multiplexer #(.select(2), .enable("false")) multiplexer_19 (
    .in0(1'b0), .in1(1'b1), .in2(1'b1), .in3(1'b0), .out(Z3), .sel(multiplexer_17_out));
  Multiplexer #(.select(2), .enable("false")) multiplexer_20 (
    .in0(1'b0), .in1(1'b0), .in2(1'b0), .in3(1'b1), .out(multiplexer_20_out), .sel(multiplexer_17_out));
  nand nand_5 (nand_5_out[0], B0, A3);
  and and_3 (nand_5_out[1], A2, B1);
  not not_7 (not_7_out, multiplexer_22_out);
  Multiplexer #(.select(2), .enable("false")) multiplexer_21 (
    .in0(multiplexer_26_out), .in1(not_9_out), .in2(not_9_out), .in3(multiplexer_26_out), .out(and_6_out[1]),
    .sel(and_5_out));
  Multiplexer #(.select(2), .enable("false")) multiplexer_22 (
    .in0(1'b0), .in1(multiplexer_26_out), .in2(multiplexer_26_out), .in3(1'b1), .out(multiplexer_22_out),
    .sel(and_5_out));
  and and_4 (and_4_out[0], A1, B2);
  not not_8 (not_8_out, multiplexer_24_out);
  Multiplexer #(.select(2), .enable("false")) multiplexer_23 (
    .in0(1'b0), .in1(1'b1), .in2(1'b1), .in3(1'b0), .out(Z2), .sel(and_6_out));
  Multiplexer #(.select(2), .enable("false")) multiplexer_24 (
    .in0(1'b0), .in1(1'b0), .in2(1'b0), .in3(1'b1), .out(multiplexer_24_out), .sel(and_6_out));
  nand nand_6 (multiplexer_17_out[1], A0, B3);
  and and_5 (and_5_out[0], B0, A2);
  not not_9 (not_9_out, multiplexer_26_out);
  and and_6 (and_6_out[0], A0, B2);
  and and_7 (and_5_out[1], A1, B1);
  Multiplexer #(.select(2), .enable("false")) multiplexer_25 (
    .in0(1'b0), .in1(1'b1), .in2(1'b1), .in3(1'b0), .out(Z1), .sel(and_9_out));
  Multiplexer #(.select(2), .enable("false")) multiplexer_26 (
    .in0(1'b0), .in1(1'b0), .in2(1'b0), .in3(1'b1), .out(multiplexer_26_out), .sel(and_9_out));
  and and_8 (and_9_out[1], B0, A1);
  and and_9 (and_9_out[0], A0, B1);
  and and_10 (Z0, B0, A0);
endmodule
