// Logisim project Logisim.circ as structural Verilog: 5 circuits, main circuit main
module main (
);

  _4_bit_synchronous_counter u_4_bit_synchronous_counter_1 ();  // open: Q3, Q2, Q1, Q0
endmodule

module Flip_Flop_JK (
  input  PRESET,
  input  J,
  input  K,
  input  RESET,
  output Q,
  output Q_prime
);

  wire CLK_out, nand_1_out, nand_2_out;

  Clock CLK (.out(CLK_out));
  nand nand_1 (nand_1_out, J, CLK_out, Q_prime);
  nand nand_2 (nand_2_out, Q, CLK_out, K);
  nand nand_3 (Q, PRESET, nand_1_out, Q_prime);
  nand nand_4 (Q_prime, Q, nand_2_out, RESET);
endmodule

module _4_bit_synchronous_counter (
  output Q3,
  output Q2,
  output Q1,
  output Q0
);

  wire and_1_out, and_2_out, clock_1_out;

  Clock clock_1 (.out(clock_1_out));
  J_K_Flip_Flop j_k_ff_1 (.J(1'b1), .clk(clock_1_out), .K(1'b1), .Q(Q0));  // open: Qn, preset, en, reset
  J_K_Flip_Flop j_k_ff_2 (.J(Q0), .clk(clock_1_out), .K(Q0), .Q(Q1));  // open: Qn, preset, en, reset
  and and_1 (and_1_out, Q0, Q1);
  J_K_Flip_Flop j_k_ff_3 (.J(and_1_out), .clk(clock_1_out), .K(and_1_out), .Q(Q2));  // open: Qn, preset, en, reset
  and and_2 (and_2_out, and_1_out, Q2);
  J_K_Flip_Flop j_k_ff_4 (.J(and_2_out), .clk(clock_1_out), .K(and_2_out), .Q(Q3));  // open: Qn, preset, en, reset
endmodule

module Decade_counter (
  input  Enable,
  input  CLK,
  input  UP_DOWN,
  output out_4,
  output out_5,
  output out_6,
  output out_7,
  output Reach_9_0
);

  wire and_1_out, and_2_out, and_3_out, and_4_out, and_5_out, and_6_out, and_7_out, and_8_out, j_k_ff_1_qn,
       j_k_ff_2_qn, j_k_ff_3_qn, not_1_out, not_2_out, not_3_out, not_4_out, not_5_out, not_6_out, not_7_out,
       not_8_out, not_9_out, or_1_out, or_2_out, or_3_out, or_4_out, or_5_out, Reset_D_out, Reset_U_out;

  not not_1 (not_1_out, UP_DOWN);
  not not_2 (not_2_out, out_4);
  not not_3 (not_3_out, UP_DOWN);
  not not_4 (not_4_out, out_6);
  J_K_Flip_Flop j_k_ff_1 (
    .J(1'b1), .clk(CLK), .K(1'b1), .Q(out_4), .Qn(j_k_ff_1_qn), .preset(Reset_D_out), .en(Enable),
    .reset(Reset_U_out));
  and Reset_D (Reset_D_out, out_4, out_5, UP_DOWN, out_6, out_7);
  and Reset_U (Reset_U_out, not_2_out, out_5, not_3_out, not_4_out, out_7);
  and and_1 (and_1_out, not_1_out, out_4);
  or or_1 (or_1_out, and_1_out, and_2_out);
  and and_2 (and_2_out, j_k_ff_1_qn, UP_DOWN);
  J_K_Flip_Flop j_k_ff_2 (
    .J(or_1_out), .clk(CLK), .K(or_1_out), .Q(out_5), .Qn(j_k_ff_2_qn), .en(Enable), .reset(or_2_out));  // open: preset
  or or_2 (or_2_out, Reset_U_out, Reset_D_out);
  and and_3 (and_3_out, and_1_out, out_5);
  or or_3 (or_3_out, and_3_out, and_4_out);
  and and_4 (and_4_out, j_k_ff_2_qn, and_2_out);
  J_K_Flip_Flop j_k_ff_3 (
    .J(or_3_out), .clk(CLK), .K(or_3_out), .Q(out_6), .Qn(j_k_ff_3_qn), .en(Enable), .reset(or_4_out));  // open: preset
  or or_4 (or_4_out, Reset_D_out, Reset_U_out);
  and and_5 (and_5_out, and_3_out, out_6);
  or or_5 (or_5_out, and_5_out, and_6_out);
  and and_6 (and_6_out, j_k_ff_3_qn, and_4_out);
  J_K_Flip_Flop j_k_ff_4 (
    .J(or_5_out), .clk(CLK), .K(or_5_out), .Q(out_7), .preset(Reset_D_out), .en(Enable), .reset(Reset_U_out));  // open: Qn
  not not_5 (not_5_out, UP_DOWN);
  and and_7 (and_7_out, or_1_out, not_5_out, out_7);
  not not_6 (not_6_out, out_4);
  not not_7 (not_7_out, out_5);
  not not_8 (not_8_out, out_6);
  not not_9 (not_9_out, out_7);
  and and_8 (and_8_out, not_6_out, not_7_out, UP_DOWN, not_8_out, not_9_out);
  or or_6 (Reach_9_0, and_7_out, and_8_out);

  // Other names for the same wires on the sheet: _1 = out_4; _2 = out_5; _4 = out_6; _8 = out_7; U_D = UP_DOWN

  // Notes on the sheet:
  //   UP (LOW)
  //   DOWN (HIGH)
endmodule

module Hundred_Counter (
  input  U_D,
  output out_2,
  output out_3,
  output out_4,
  output out_5,
  output out_6,
  output out_7,
  output out_8,
  output out_9
);

  wire clock_1_out, decade_counter_1_reach_9_0;

  Clock clock_1 (.out(clock_1_out));
  Decade_counter decade_counter_1 (
    .UP_DOWN(U_D), .Reach_9_0(decade_counter_1_reach_9_0), .Enable(1'b1), .out_4(out_9), .out_5(out_8),
    .out_6(out_7), .out_7(out_6), .CLK(clock_1_out));
  Decade_counter decade_counter_2 (
    .UP_DOWN(U_D), .Enable(decade_counter_1_reach_9_0), .out_4(out_5), .out_5(out_4), .out_6(out_3),
    .out_7(out_2), .CLK(clock_1_out));  // open: Reach_9_0
endmodule
