// Logisim project Decoder 7 segmentos.circ as structural Verilog: 2 circuits, main circuit main
// b
module main (
  input  [3:0] Din0,
  input  PD,
  input  in_3,
  input  [3:0] Din1,
  input  PD_2,
  input  [3:0] Din2,
  input  PD_3,
  input  [3:0] Din3,
  input  PD_4
);

  wire a, and_5_out, and_6_out, and_7_out, and_8_out, and_9_out, and_10_out, and_11_out, and_12_out,
       and_13_out, and_14_out, and_15_out, and_16_out, and_17_out, and_18_out, and_19_out, and_20_out,
       and_21_out, and_22_out, and_23_out, and_24_out, and_25_out, and_26_out, and_27_out, and_28_out,
       and_29_out, and_30_out, and_31_out, and_32_out, and_33_out, and_34_out, and_35_out, and_36_out,
       and_37_out, and_38_out, and_39_out, and_40_out, and_41_out, and_42_out, and_43_out, and_44_out,
       and_45_out, and_46_out, and_47_out, and_48_out, and_49_out, and_50_out, and_51_out, and_52_out, b, c,
       clock_1_out, d, D0, D1, D2, D3, e, f, g, i0, i1, i2, i3, PD0, PD1, PD2, PD3, PDi, PDo, Q0, Q1,
       undriven, undriven_2, undriven_3, undriven_4;

  Clock clock_1 (.out(clock_1_out));
  and and_1 (PD0, D0, PD);
  and and_2 (PD1, D1, PD_2);
  and and_3 (PD2, D2, PD_3);
  and and_4 (PD3, D3, PD_4);
  J_K_Flip_Flop j_k_ff_1 (.J(1'b1), .clk(clock_1_out), .K(1'b1), .Q(Q0));  // open: Qn, preset, en, reset
  and and_5 (and_5_out, D0, Din0[0]);
  and and_6 (and_6_out, Din0[1], D0);
  and and_7 (and_7_out, Din0[2], D0);
  and and_8 (and_8_out, D0, Din0[3]);
  and and_9 (and_9_out, D1, Din1[0]);
  and and_10 (and_10_out, Din1[1], D1);
  and and_11 (and_11_out, Din1[2], D1);
  and and_12 (and_12_out, D1, Din1[3]);
  and and_13 (and_13_out, D2, Din2[0]);
  and and_14 (and_14_out, Din2[1], D2);
  and and_15 (and_15_out, Din2[2], D2);
  and and_16 (and_16_out, D2, Din2[3]);
  and and_17 (and_17_out, D3, Din3[0]);
  and and_18 (and_18_out, Din3[1], D3);
  and and_19 (and_19_out, Din3[2], D3);
  and and_20 (and_20_out, D3, Din3[3]);
  J_K_Flip_Flop j_k_ff_2 (.J(Q0), .clk(clock_1_out), .K(Q0), .Q(Q1));  // open: Qn, preset, en, reset
  Decoder #(.select(2), .enable("false")) decoder_1 (.out0(D0), .out1(D1), .out2(D2), .out3(D3), .sel({Q1, Q0}));
  or or_1 (i0, and_5_out, and_9_out, and_13_out, and_17_out);
  or or_2 (i1, and_6_out, and_10_out, and_14_out, and_18_out);
  or or_3 (i2, and_7_out, and_11_out, and_15_out, and_19_out);
  or or_4 (i3, and_8_out, and_12_out, and_16_out, and_20_out);
  _7_Segment_Display u_7_segment_display_1 (
    .e(undriven), .d(undriven_2), .c(undriven_3), .dp(undriven_4));  // open: g, f, a, b
  Multiplexer #(.select(2), .enable("false")) multiplexer_1 (
    .in0(PD0), .in1(PD1), .in2(PD2), .in3(PD3), .out(PDi), .sel({Q1, Q0}));
  and and_21 (and_21_out, g, D3);
  and and_22 (and_22_out, f, D3);
  and and_23 (and_23_out, a, D3);
  _7_Segment_Display u_7_segment_display_2 (
    .g(and_21_out), .f(and_22_out), .a(and_23_out), .b(and_27_out), .e(and_26_out), .d(and_25_out),
    .c(and_24_out), .dp(and_30_out));
  and and_24 (and_24_out, D3, c);
  and and_25 (and_25_out, D3, d);
  and and_26 (and_26_out, D3, e);
  and and_27 (and_27_out, b, D3);
  and and_28 (and_28_out, g, D2);
  and and_29 (and_29_out, D2, e);
  and and_30 (and_30_out, D3, PDo);
  and and_31 (and_31_out, b, D2);
  and and_32 (and_32_out, f, D2);
  and and_33 (and_33_out, a, D2);
  _7_Segment_Display u_7_segment_display_3 (
    .g(and_28_out), .f(and_32_out), .a(and_33_out), .b(and_31_out), .e(and_29_out), .d(and_34_out),
    .c(and_36_out), .dp(and_35_out));
  and and_34 (and_34_out, D2, d);
  and and_35 (and_35_out, D2, PDo);
  and and_36 (and_36_out, D2, c);
  Unidad unidad_1 (
    .I3(i3), .I2(i2), .I1(i1), .I0(i0), .out_14(PDo), .out_7(a), .out_8(f), .out_9(b), .out_10(g),
    .out_11(e), .out_12(c), .out_13(d), .Punto_decimal(PDi), .Enable(in_3));
  and and_37 (and_37_out, f, D1);
  and and_38 (and_38_out, g, D1);
  _7_Segment_Display u_7_segment_display_4 (
    .g(and_38_out), .f(and_37_out), .a(and_41_out), .b(and_42_out), .e(and_39_out), .d(and_40_out),
    .c(and_44_out), .dp(and_43_out));
  and and_39 (and_39_out, D1, e);
  and and_40 (and_40_out, D1, d);
  and and_41 (and_41_out, a, D1);
  and and_42 (and_42_out, b, D1);
  and and_43 (and_43_out, D1, PDo);
  and and_44 (and_44_out, D1, c);
  and and_45 (and_45_out, f, D0);
  and and_46 (and_46_out, g, D0);
  _7_Segment_Display u_7_segment_display_5 (
    .g(and_46_out), .f(and_45_out), .a(and_50_out), .b(and_49_out), .e(and_48_out), .d(and_47_out),
    .c(and_51_out), .dp(and_52_out));
  and and_47 (and_47_out, D0, d);
  and and_48 (and_48_out, D0, e);
  and and_49 (and_49_out, b, D0);
  and and_50 (and_50_out, a, D0);
  and and_51 (and_51_out, D0, c);
  and and_52 (and_52_out, D0, PDo);

  // Notes on the sheet:
  //   COUNTER
  //   SELECTOR DE ENTRADA
  //   DECODER 7S
endmodule

module Unidad (
  input  Punto_decimal,
  input  I3,
  input  I2,
  input  I1,
  input  I0,
  input  Enable,
  output out_7,
  output out_8,
  output out_9,
  output out_10,
  output out_11,
  output out_12,
  output out_13,
  output out_14
);

  wire and_1_out, and_2_out, and_3_out, and_4_out, and_5_out, and_6_out, and_7_out, and_8_out, and_9_out,
       not_1_out, not_2_out, not_3_out, or_1_out, or_2_out, or_3_out, or_4_out, or_5_out, or_6_out, or_7_out;

  not not_1 (not_1_out, I2);
  not not_2 (not_2_out, I0);
  not not_3 (not_3_out, I1);
  and and_1 (and_1_out, I2, I0);
  and and_2 (and_2_out, not_1_out, not_2_out);
  and and_3 (and_3_out, I1, I0);
  and and_4 (and_4_out, not_3_out, not_2_out);
  and and_5 (and_5_out, I1, not_2_out);
  and and_6 (and_6_out, not_1_out, I1);
  and and_7 (and_7_out, I0, and_8_out);
  and and_8 (and_8_out, I2, not_3_out);
  and and_9 (and_9_out, I2, not_2_out);
  and and_10 (out_7, Enable, or_1_out);
  or or_1 (or_1_out, and_1_out, and_2_out, I3, I1);
  and and_11 (out_9, Enable, or_2_out);
  or or_2 (or_2_out, and_3_out, and_4_out, not_1_out);
  and and_12 (out_12, Enable, or_3_out);
  or or_3 (or_3_out, I2, not_3_out, I0);
  and and_13 (out_13, Enable, or_4_out);
  or or_4 (or_4_out, I3, and_2_out, and_5_out, and_6_out, and_7_out);
  and and_14 (out_11, Enable, or_5_out);
  or or_5 (or_5_out, and_5_out, and_2_out);
  and and_15 (out_8, Enable, or_6_out);
  or or_6 (or_6_out, and_4_out, and_9_out, and_8_out, I3);
  and and_16 (out_10, Enable, or_7_out);
  or or_7 (or_7_out, and_5_out, and_8_out, I3, and_6_out);
  _7_Segment_Display u_7_segment_display_1 (
    .g(out_10), .f(out_8), .a(out_7), .b(out_9), .e(out_11), .d(out_13), .c(out_12), .dp(Punto_decimal));

  assign out_14 = Punto_decimal;

  // Other names for the same wires on the sheet: a = out_7; b = out_9; c = out_12; d = out_13; e = out_11; f = out_8;
  //   g = out_10; PD = Punto_decimal
endmodule
