// Logisim project Esquematico.circ as structural Verilog: 3 circuits, main circuit main
module main (
  input  [7:0] in_1,
  input  in_2,
  input  [7:0] in_3
);

  FullAdder_8bits fulladder_8bits_1 (
    .A(in_1), .T(in_2), .B(in_3));  // open: C_FLAG, OV_FLAG, out_5, out_6, out_7, out_8, out_9, out_10, out_11, out_12
endmodule

module FullAdder_1bit (
  input  A,
  input  B,
  input  C,
  output R,
  output Co
);

  wire and_1_out, and_2_out, xor_1_out;

  xor xor_1 (xor_1_out, A, B);
  and and_1 (and_1_out, C, xor_1_out);
  and and_2 (and_2_out, A, B);
  xor xor_2 (R, xor_1_out, C);
  or or_1 (Co, and_1_out, and_2_out);
endmodule

module FullAdder_8bits (
  input  [7:0] A,
  input  T,
  input  [7:0] B,
  output C_FLAG,
  output out_5,
  output out_6,
  output out_7,
  output out_8,
  output out_9,
  output out_10,
  output out_11,
  output out_12,
  output OV_FLAG
);

  wire fulladder_1bit_1_co, fulladder_1bit_2_co, fulladder_1bit_3_co, fulladder_1bit_4_co,
       fulladder_1bit_5_co, fulladder_1bit_6_co, fulladder_1bit_7_co, xor_1_out, xor_2_out, xor_3_out,
       xor_4_out, xor_5_out, xor_6_out, xor_7_out, xor_8_out;

  FullAdder_1bit fulladder_1bit_1 (.A(A[0]), .B(xor_1_out), .C(T), .R(out_12), .Co(fulladder_1bit_1_co));
  xor xor_1 (xor_1_out, T, B[0]);
  xor xor_2 (xor_2_out, T, B[1]);
  FullAdder_1bit fulladder_1bit_2 (
    .A(A[1]), .B(xor_2_out), .C(fulladder_1bit_1_co), .R(out_11), .Co(fulladder_1bit_2_co));
  xor xor_3 (xor_3_out, T, B[2]);
  FullAdder_1bit fulladder_1bit_3 (
    .A(A[2]), .B(xor_3_out), .C(fulladder_1bit_2_co), .R(out_10), .Co(fulladder_1bit_3_co));
  xor xor_4 (xor_4_out, T, B[3]);
  FullAdder_1bit fulladder_1bit_4 (
    .A(A[3]), .B(xor_4_out), .C(fulladder_1bit_3_co), .R(out_9), .Co(fulladder_1bit_4_co));
  xor xor_5 (xor_5_out, T, B[4]);
  FullAdder_1bit fulladder_1bit_5 (
    .A(A[4]), .B(xor_5_out), .C(fulladder_1bit_4_co), .R(out_8), .Co(fulladder_1bit_5_co));
  FullAdder_1bit fulladder_1bit_6 (
    .A(A[5]), .B(xor_6_out), .C(fulladder_1bit_5_co), .R(out_7), .Co(fulladder_1bit_6_co));
  xor xor_6 (xor_6_out, T, B[5]);
  xor xor_7 (xor_7_out, T, B[6]);
  FullAdder_1bit fulladder_1bit_7 (
    .A(A[6]), .B(xor_7_out), .C(fulladder_1bit_6_co), .R(out_6), .Co(fulladder_1bit_7_co));
  xor xor_8 (xor_8_out, T, B[7]);
  FullAdder_1bit fulladder_1bit_8 (.A(A[7]), .B(xor_8_out), .C(fulladder_1bit_7_co), .R(out_5), .Co(C_FLAG));
  xor xor_9 (OV_FLAG, C_FLAG, fulladder_1bit_7_co);

  // Other names for the same wires on the sheet: R0 = out_12; R1 = out_11; R2 = out_10; R3 = out_9; R4 = out_8;
  //   R5 = out_7; R6 = out_6; R7 = out_5
endmodule
